# Fritzing sketch 0400_Capacitor_Charging_Discharging (saved by Fritzing 0.9.6b)
breadboards: 1

parts:
  X1 = Arduino Uno (Rev3) - ICSP
  LED1 = LED - 5mm [color="Red (633nm)" current=0.030 package="5 mm [THT]"]
  R2 = Resistor [tolerance=±5% power=0.25 resistance=220 package=THT]
  R1 = Trimmer Potentiometer [maximum_resistance=10kΩ package=THT]
  C1 = Capacitor Polarized [part_number="10 uF" package=cpol-radial-10uf-25v]
  R3 = Resistor [tolerance=±2% power=0.25 resistance=100k package=THT]

nets:
  N1: X1.A0, R1.wiper
  V_cap: X1.A5/SCL, X1.D7, C1.+, R3.Pin_0
  N2: X1.ICSP_MOSI, X1.D11_PWM/MOSI, LED1.anode
  N3: X1.D9_PWM, R3.Pin_1
  5V: X1.5V, R1.leg2
  GND: X1.GND, R2.Pin_0, R1.leg1, C1.-
  N4: LED1.cathode, R2.Pin_1
